# Fritzing sketch redboard_esp8266_pwr_fritzing_sketch (saved by Fritzing 0.9.2b)
breadboards: 1

parts:
  YwRobot_Power_Supply1 = YwRobot Breadboard Power Supply [part_number=545043]
  Parts1 = SparkFun RedBoard [part_number=DEV-12757]
  part = ESP8266 WiFi Module [part_number=ESP8266]
  Logic_Level_Converter = Bi-Directional Logic Level Converter [part_number="BOB 12009"]

nets:
  N1: YwRobot_Power_Supply1.VCC#10, part.VCC, part.RST, part.CH_PD, Logic_Level_Converter.LV
  N2: YwRobot_Power_Supply1.GND#12, Parts1.GND, Parts1.RESET, Logic_Level_Converter.GND#8
  N3: YwRobot_Power_Supply1.GND#14, part.GND, Logic_Level_Converter.GND#3
  N4: Parts1.D0/RX, Logic_Level_Converter.HV1
  N5: Parts1.D1/TX, Logic_Level_Converter.HV2
  N6: Parts1.5V, Logic_Level_Converter.HV
  N7: part.RXD, Logic_Level_Converter.LV1
  N8: part.TXD, Logic_Level_Converter.LV2

notes:
  CHPD
  RST
  VCC
  GND
  RXD
  TXD
  Set power supply
  to 3.3 V
  ESP8266
  VCC --> +3.3V
  RST --> +3.3V
  CHPD --> +3.3V
  GND --> GND
  RXD --> LV1
  TXD --> LV2

custom parts:
  YwRobot Breadboard Power Supply: The YwRobot Breadboard Power Supply (MB-V2) has two power rails; they can be 5V or 3V3. Power to the module can be provided through the female USB socket or through the A10 (female) 2.1mm power jack.
  SparkFun RedBoard: At SparkFun we use many Arduinos and we’re always looking for the simplest, most stable one. Each board is a bit different and no one board has everything we want, so we decided to make our own version that combines all our favorite features. The RedBoard combines the simplicity of the UNO’s Optiboot bootloader (which is used in the Pro series), the stability of the FTDI (which we all missed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
  ESP8266 WiFi Module: Generic WiFi Module based on the ESP8266 with onboard PCB antenna and UART communications
  Bi-Directional Logic Level Converter: Description: If you've ever tried to connect a 3.3V device to a 5V system, you know what a challenge it can be. The SparkFun bi-directional logic level converter is a small device that safely steps down 5V signals to 3.3V AND steps up 3.3V to 5V at the same time. This level converter also works with 2.8V and 1.8V devices. What really separates this Logic level converter from our previous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
